# Fritzing sketch Laser Viscometer (saved by Fritzing 0.9.3b)
circuit board: 8.46667cm x 5.64444cm
breadboards: 1

parts:
  Part1 = Arduino Nano (Rev3.0)
  S1 = Pushbutton [package="[THT]"]
  R1 = Resistor [tolerance=±5% resistance=100k package=THT]
  R2 = Resistor [tolerance=±5% resistance=100k package=THT]
  R3 = Resistor [tolerance=±5% resistance=100k package=THT]
  LD1 = LD
  LD2 = LD
  LED1 = LED - 5mm [color="White (8000K)" package="5 mm [THT]"]
  LED2 = LED - 5mm [color="White (8000K)" package="5 mm [THT]"]

nets:
  N1: Part1.GND, R1.Pin_1, R2.Pin_1, R3.Pin_1, LD1.cathode, LD2.cathode
  N2: Part1.D2, R3.Pin_0, LED1.cathode
  N3: Part1.D3, R2.Pin_0, LED2.cathode
  N4: Part1.D4, S1.Pin_3, S1.Pin_4, R1.Pin_0
  N5: Part1.5V, S1.Pin_1, S1.Pin_2, LED1.anode, LED2.anode
  N6: Part1.D13/SCK, LD1.anode, LD2.anode

custom parts:
  LD: A Generic Red Dot Laser Diode Module (~5mW)
